# Fritzing sketch schema_2b3l (saved by Fritzing 0.9.2b)
breadboards: 1

parts:
  Raspberry_Pi1 = Raspberry Pi 2
  LED1 = LED - 5mm [color="Red (633nm)" package="5 mm [THT]"]
  LED2 = LED - 5mm [color="Yellow (595nm)" package="5 mm [THT]"]
  LED3 = LED - 5mm [color="Green (560nm)" package="5 mm [THT]"]
  R1 = Resistor [tolerance=±5% resistance=68 package=THT]
  R2 = Resistor [tolerance=±5% resistance=68 package=THT]
  R3 = Resistor [tolerance=±5% resistance=68 package=THT]
  S1 = Pushbutton [package="[THT]"]
  S2 = Pushbutton [package="[THT]"]

nets:
  N1: Raspberry_Pi1.GPIO19, S2.Pin_3, S2.Pin_4
  N2: Raspberry_Pi1.GPIO26, S1.Pin_3, S1.Pin_4
  N3: Raspberry_Pi1.GND, LED1.cathode, LED2.cathode, LED3.cathode, S1.Pin_1, S1.Pin_2, S2.Pin_1, S2.Pin_2
  N4: Raspberry_Pi1.GPIO21, R1.Pin_1
  N5: Raspberry_Pi1.GPIO20, R2.Pin_1
  N6: Raspberry_Pi1.GPIO16, R3.Pin_0
  N7: LED1.anode, R1.Pin_0
  N8: LED2.anode, R2.Pin_0
  N9: LED3.anode, R3.Pin_1
